# Fritzing sketch autotuner (saved by Fritzing 1.0.1rc)
breadboards: 1

parts:
  SOM1 = Daisy Seed [chip_label=IC package="DIP (Dual Inline) [THT]"]
  MIC1 = Microphone
  SP1 = SPEAKER [package=pcb_mount_speaker]
  JP1 = Header 12 [package=1x12_machine-pin-header_lock.004]  # not connected
  JP2 = Header 12 [package=1x12_machine-pin-header_lock.004]
  U3 = POT [knob_status=50% package=pot_alpha_rv16af-20]
  U4 = POT [knob_status=50% package=pot_mammoth]

nets:
  N1: SOM1.pin_16, JP2.2
  N2: SOM1.pin_18, SP1.-
  GND: SOM1.pin_20, SOM1.pin_40, SP1.+, JP2.1
  N3: MIC1.pin1, JP2.11
  N4: MIC1.pin2, JP2.12
  N5: JP2.3, U4.S
  N6: JP2.4, U4.A
  N7: JP2.5, U4.E
  N8: JP2.6, U3.A
  N9: JP2.7, U3.S
  N10: JP2.8, U3.E
  N11: JP2.9, JP2.10

custom parts:
  Daisy Seed: Daisy is an embedded platform for music. It features everything you need for creating high fidelity audio hardware devices. Just plug in a USB cable and start making sound! No soldering required.
  Header 12: Header 12 Standard 12-pin 0.1 header. Use with straight break away headers (SKU : PRT-00116), right angle break away headers (PRT-00553), swiss pins (PRT-00743), machine pins (PRT-00117), and female headers (PRT-00115).
